// Logisim project MiniCounter.circ as structural Verilog: 20 circuits, main circuit 数码管驱动
// LED计数
module \LED计数电路  (
);


  // Notes on the sheet:
  //   此电路空白，需要你从头绘制！
endmodule

module \LED计数测试  (
);


  // Notes on the sheet:
  //   此电路空白，需要你从头绘制！
endmodule

// 编码器
module \_5输入编码器  (
  input  In1,
  input  In2,
  input  In3,
  input  In4,
  input  In5,
  output Out1,
  output Out2,
  output Out3
);

  wire and_1_out, and_2_out, and_3_out, and_4_out, not_1_out, not_2_out, not_3_out, not_4_out, not_5_out,
       not_6_out, not_7_out;

  and and_1 (and_1_out, In3, not_1_out);
  not not_1 (not_1_out, In4);
  and and_2 (and_2_out, In1, not_2_out, not_3_out);
  not not_2 (not_2_out, In2);
  not not_3 (not_3_out, In4);
  and and_3 (and_3_out, In3, not_4_out, not_5_out);
  not not_4 (not_4_out, In4);
  not not_5 (not_5_out, In5);
  and and_4 (and_4_out, In2, not_6_out, not_7_out);
  not not_6 (not_6_out, In4);
  not not_7 (not_7_out, In5);
  or or_1 (Out3, In5, In4);
  or or_2 (Out1, In5, and_1_out, and_2_out);
  or or_3 (Out2, and_3_out, and_4_out);

  // Notes on the sheet:
  //   此电路空白，需要你从头绘制！
endmodule

module \数码管驱动  (
  input  X3,
  input  X2,
  input  X1,
  input  X0,
  output Seg_1,
  output Seg_2,
  output Seg_3,
  output Seg_4,
  output Seg_5,
  output Seg_6,
  output Seg_7
);

  wire and_1_out, and_2_out, and_3_out, and_4_out, and_5_out, and_6_out, and_7_out, and_8_out, and_9_out,
       and_10_out, and_11_out, and_12_out, and_13_out, and_14_out, and_15_out, and_16_out, and_17_out,
       and_18_out, and_19_out, and_20_out, and_21_out, and_22_out, and_23_out, and_24_out, and_25_out,
       and_26_out, and_27_out, and_28_out, and_29_out, and_30_out, and_31_out, and_32_out, and_33_out,
       and_34_out, and_35_out, not_1_out, not_2_out, not_3_out, not_4_out, not_5_out, not_6_out, not_7_out,
       not_8_out, not_9_out, not_10_out, not_11_out, not_12_out, not_13_out, not_14_out, not_15_out,
       not_16_out, not_17_out, not_18_out, not_19_out, not_20_out, not_21_out, not_22_out, not_23_out,
       not_24_out, not_25_out, not_26_out, not_27_out, not_28_out, not_29_out, not_30_out, not_31_out,
       not_32_out, not_33_out, not_34_out, not_35_out, not_36_out, not_37_out, not_38_out, not_39_out,
       not_40_out, not_41_out, not_42_out, not_43_out;

  not not_1 (not_1_out, X2);
  and and_1 (and_1_out, not_1_out, X1);
  and and_2 (and_2_out, X1, not_2_out);
  not not_2 (not_2_out, X0);
  not not_3 (not_3_out, X3);
  and and_3 (and_3_out, not_3_out, X2, not_4_out);
  not not_4 (not_4_out, X1);
  and and_4 (and_4_out, X3, not_5_out);
  not not_5 (not_5_out, X2);
  and and_5 (and_5_out, X3, X0);
  not not_6 (not_6_out, X1);
  and and_6 (and_6_out, not_6_out, not_7_out);
  not not_7 (not_7_out, X0);
  not not_8 (not_8_out, X3);
  and and_7 (and_7_out, not_8_out, X2, not_9_out);
  not not_9 (not_9_out, X1);
  and and_8 (and_8_out, X2, not_10_out);
  not not_10 (not_10_out, X0);
  and and_9 (and_9_out, X3, not_11_out);
  not not_11 (not_11_out, X2);
  and and_10 (and_10_out, X3, X1);
  not not_12 (not_12_out, X2);
  and and_11 (and_11_out, not_12_out, not_13_out);
  not not_13 (not_13_out, X0);
  not not_14 (not_14_out, X3);
  and and_12 (and_12_out, not_14_out, X1);
  not not_15 (not_15_out, X3);
  and and_13 (and_13_out, not_15_out, X2, X0);
  and and_14 (and_14_out, X2, X1);
  and and_15 (and_15_out, X3, not_16_out, not_17_out);
  not not_16 (not_16_out, X2);
  not not_17 (not_17_out, X1);
  and and_16 (and_16_out, X3, not_18_out);
  not not_18 (not_18_out, X0);
  not not_19 (not_19_out, X3);
  and and_17 (and_17_out, not_19_out, not_20_out);
  not not_20 (not_20_out, X2);
  not not_21 (not_21_out, X3);
  and and_18 (and_18_out, not_21_out, not_22_out, not_23_out);
  not not_22 (not_22_out, X1);
  not not_23 (not_23_out, X0);
  not not_24 (not_24_out, X2);
  and and_19 (and_19_out, not_24_out, not_25_out);
  not not_25 (not_25_out, X0);
  not not_26 (not_26_out, X3);
  and and_20 (and_20_out, not_26_out, X1, X0);
  and and_21 (and_21_out, X3, not_27_out, X0);
  not not_27 (not_27_out, X1);
  not not_28 (not_28_out, X2);
  and and_22 (and_22_out, not_28_out, not_29_out);
  not not_29 (not_29_out, X0);
  and and_23 (and_23_out, X1, not_30_out);
  not not_30 (not_30_out, X0);
  and and_24 (and_24_out, X3, X1);
  and and_25 (and_25_out, X3, X2);
  not not_31 (not_31_out, X3);
  and and_26 (and_26_out, not_31_out, not_32_out, not_33_out);
  not not_32 (not_32_out, X2);
  not not_33 (not_33_out, X0);
  not not_34 (not_34_out, X2);
  and and_27 (and_27_out, not_34_out, X1, X0);
  not not_35 (not_35_out, X1);
  and and_28 (and_28_out, X2, not_35_out, X0);
  and and_29 (and_29_out, X2, X1, not_36_out);
  not not_36 (not_36_out, X0);
  and and_30 (and_30_out, X3, not_37_out);
  not not_37 (not_37_out, X1);
  not not_38 (not_38_out, X3);
  and and_31 (and_31_out, not_38_out, not_39_out);
  not not_39 (not_39_out, X1);
  not not_40 (not_40_out, X3);
  and and_32 (and_32_out, not_40_out, X0);
  not not_41 (not_41_out, X1);
  and and_33 (and_33_out, not_41_out, X0);
  not not_42 (not_42_out, X3);
  and and_34 (and_34_out, not_42_out, X2);
  and and_35 (and_35_out, X3, not_43_out);
  not not_43 (not_43_out, X2);
  or or_1 (Seg_1, and_1_out, and_2_out, and_3_out, and_4_out, and_5_out);
  or or_2 (Seg_2, and_6_out, and_7_out, and_8_out, and_9_out, and_10_out);
  or or_3 (Seg_4, and_17_out, and_18_out, and_19_out, and_20_out, and_21_out);
  or or_4 (Seg_5, and_22_out, and_23_out, and_24_out, and_25_out);
  or or_5 (Seg_6, and_26_out, and_27_out, and_28_out, and_29_out, and_30_out);
  or or_6 (Seg_7, and_31_out, and_32_out, and_33_out, and_34_out, and_35_out);
  or or_7 (Seg_3, and_11_out, and_12_out, and_13_out, and_14_out, and_15_out, and_16_out);
endmodule

module \数码管驱动测试  (
);

  wire clock_1_out, \数码管驱动_1_seg_1 , \数码管驱动_1_seg_2 , \数码管驱动_1_seg_3 , \数码管驱动_1_seg_4 , \数码管驱动_1_seg_5 ,
       \数码管驱动_1_seg_6 , \数码管驱动_1_seg_7 ;
  wire [3:0] counter_1_q;

  Counter #(.width(4), .max('hf), .ongoal("wrap"), .trigger("rising"), .behavior("old")) counter_1 (
    .Q(counter_1_q), .clk(clock_1_out));  // open: load, D, count, carry, clr, preset
  Clock #(.highDuration(1), .lowDuration(1)) clock_1 (.out(clock_1_out));
  \数码管驱动  \u_数码管驱动_1  (
    .X3(counter_1_q[3]), .X2(counter_1_q[2]), .X1(counter_1_q[1]), .Seg_1(\数码管驱动_1_seg_1 ),
    .X0(counter_1_q[0]), .Seg_2(\数码管驱动_1_seg_2 ), .Seg_3(\数码管驱动_1_seg_3 ), .Seg_4(\数码管驱动_1_seg_4 ),
    .Seg_5(\数码管驱动_1_seg_5 ), .Seg_6(\数码管驱动_1_seg_6 ), .Seg_7(\数码管驱动_1_seg_7 ));
  _7_Segment_Display #(.active("true")) u_7_segment_display_1 (
    .g(\数码管驱动_1_seg_1 ), .f(\数码管驱动_1_seg_2 ), .a(\数码管驱动_1_seg_3 ), .b(\数码管驱动_1_seg_4 ), .e(\数码管驱动_1_seg_5 ),
    .d(\数码管驱动_1_seg_6 ), .c(\数码管驱动_1_seg_7 ));  // open: dp

  // Notes on the sheet:
  //   Ctrl+T驱动时钟单步运行测试
endmodule

// 4位数比较器
module \_4位无符号比较器  (
  input  X3,
  input  X2,
  input  X1,
  input  X0,
  input  Y3,
  input  Y2,
  input  Y1,
  input  Y0,
  output Great,
  output Equal,
  output Less
);

  Comparator #(.width(4), .mode("unsigned")) comparator_1 (
    .a({X3, X2, X1, X0}), .b({Y3, Y2, Y1, Y0}), .gt(Great), .eq(Equal), .lt(Less));
endmodule

module \_8位无符号比较器  (
  input  [7:0] X,
  input  [7:0] Y,
  output Great,
  output Equal,
  output Less
);

  // Probe on X
  // Probe on Y
  Comparator #(.width(8), .mode("unsigned")) comparator_1 (.a(X), .b(Y), .gt(Great), .eq(Equal), .lt(Less));

  // Other names for the same wires on the sheet: X0[3:0] = X[3:0]; X1[3:0] = X[7:4]; Y0[3:0] = Y[3:0];
  //   Y1[3:0] = Y[7:4]

  // Notes on the sheet:
  //   请勿增删改引脚，否则可能导致电路封装变化，无法测试
  //   请勿增删改引脚，请在下方利用上方输入输出引脚的隧道标签信号构建电路，ctrl+d复制选择组件
  //   电路功能：X,Y进行无符号比较，Great=(X>Y)?1:0;
  //   输出引脚区
endmodule

// MUX
module \_2路选择器_1位  (
  input  X0,
  input  Sel,
  input  X1,
  output Out
);

  Multiplexer #(.select(1), .width(1), .disabled("Z"), .enable("false")) multiplexer_1 (
    .in0(X0), .in1(X1), .out(Out), .sel(Sel));

  // Notes on the sheet:
  //   请勿增删改引脚，否则可能导致电路封装变化，无法测试
  //   请勿增删改引脚，请在下方利用上方输入输出引脚的隧道标签信号构建电路，ctrl+d复制选择组件
  //   输入引脚区
  //   输出引脚区
  //   电路功能：Out=(Sel==0)?X0:X1;
endmodule

// MUX
module \_2路选择器_4位  (
  input  [3:0] X,
  input  Sel,
  input  [3:0] Y,
  output [3:0] Out
);

  // Probe on X
  // Probe on Y
  Multiplexer #(.select(1), .width(4), .disabled("Z"), .enable("false")) multiplexer_1 (
    .in0(X), .in1(Y), .out(Out), .sel(Sel));
  // Probe on Out

  // Notes on the sheet:
  //   请勿增删改引脚，否则可能导致电路封装变化，无法测试！
  //   请勿增删改引脚，请在下方利用上方输入输出引脚的隧道标签信号构建电路，ctrl+d复制选择组件
  //   输入引脚区
  //   电路功能：Out=(Sel==0)?X:Y;
  //   输出引脚区
endmodule

// BCD计数
module \BCD双向计数器_可异步置位  (
  input  CLK,
  input  \使能 ,
  input  \异步置位 ,
  input  [3:0] \预置数据 ,
  input  \计数模式 ,
  input  \复位 ,
  output [3:0] \输出Q ,
  output \进位_借位 
);

  wire D0, D1, D2, D3, not_1_out, not_2_out, not_3_out, not_4_out, or_1_out;
  wire [3:0] \bcd双向计数器状态转换_自动生成_1_n0 , \n2路选择器_4位_1_out ;

  Pull_Resistor #(.pull(0)) pull_resistor_1 (.node(\异步置位 ));
  Pull_Resistor #(.pull(0)) pull_resistor_2 (.node(\计数模式 ));
  \BCD双向计数器状态转换_自动生成  \bcd双向计数器状态转换_自动生成_1  (
    .S3(\输出Q [3]), .S2(\输出Q [2]), .S1(\输出Q [1]), .S0(\输出Q [0]), .N3(\bcd双向计数器状态转换_自动生成_1_n0 [3]),
    .Mode(\计数模式 ), .N2(\bcd双向计数器状态转换_自动生成_1_n0 [2]), .N1(\bcd双向计数器状态转换_自动生成_1_n0 [1]),
    .N0(\bcd双向计数器状态转换_自动生成_1_n0 [0]));
  \BCD双向计数器输出函数_自动生成  \bcd双向计数器输出函数_自动生成_1  (
    .S3(\输出Q [3]), .S2(\输出Q [2]), .S1(\输出Q [1]), .Cout(\进位_借位 ), .S0(\输出Q [0]), .Mode(\计数模式 ));
  Pull_Resistor #(.pull(1)) pull_resistor_3 (.node(\使能 ));
  Pull_Resistor #(.pull(0)) pull_resistor_4 (.node(\预置数据 ));
  Pull_Resistor #(.pull(0)) pull_resistor_5 (.node(\复位 ));
  \_2路选择器_4位  \u_2路选择器_4位_1  (.X(\预置数据 ), .Out(\n2路选择器_4位_1_out ), .Sel(\复位 ), .Y(4'b0000));
  D_Flip_Flop #(.trigger("rising"), .Pre_Clr_Positions("LEGACY"), .NegatePresetClear("false"), .enable("true"), .NewFFLayout("false")) u_D3 (
    .clk(CLK), .D(\bcd双向计数器状态转换_自动生成_1_n0 [3]), .Q(\输出Q [3]), .preset(D3), .en(\使能 ), .reset(not_1_out));  // open: Qn
  not not_1 (not_1_out, D3);
  D_Flip_Flop #(.trigger("rising"), .Pre_Clr_Positions("LEGACY"), .NegatePresetClear("false"), .enable("true"), .NewFFLayout("false")) u_D2 (
    .clk(CLK), .D(\bcd双向计数器状态转换_自动生成_1_n0 [2]), .Q(\输出Q [2]), .preset(D2), .en(\使能 ), .reset(not_2_out));  // open: Qn
  not not_2 (not_2_out, D2);
  D_Flip_Flop #(.trigger("rising"), .Pre_Clr_Positions("LEGACY"), .NegatePresetClear("false"), .enable("true"), .NewFFLayout("false")) u_D1 (
    .clk(CLK), .D(\bcd双向计数器状态转换_自动生成_1_n0 [1]), .Q(\输出Q [1]), .preset(D1), .en(\使能 ), .reset(not_3_out));  // open: Qn
  not not_3 (not_3_out, D1);
  D_Flip_Flop #(.trigger("rising"), .Pre_Clr_Positions("LEGACY"), .NegatePresetClear("false"), .enable("true"), .NewFFLayout("false")) u_D0 (
    .clk(CLK), .D(\bcd双向计数器状态转换_自动生成_1_n0 [0]), .Q(\输出Q [0]), .preset(D0), .en(\使能 ), .reset(not_4_out));  // open: Qn
  not not_4 (not_4_out, D0);
  assign {D3, D2, D1, D0} = or_1_out ? \n2路选择器_4位_1_out  : 4'bz;  // Controlled_Buffer controlled_buffer_1
  or or_1 (or_1_out, \复位 , \异步置位 );
  // Probe on \输出Q 

  // Other names for the same wires on the sheet: Cout = \进位_借位 ; Din[3:0] = \预置数据 ; En = \使能 ; Mode = \计数模式 ;
  //   PreSet = \异步置位 ; Q[3:0] = \输出Q ; RST = \复位 

  // Notes on the sheet:
  //   请勿增删改引脚，否则可能导致电路封装变化，无法测试！！！
  //   上拉下拉电阻用于给出引脚悬空的时的默认值
  //   D3D2D1D0分别接D触发器异步置位和复位端实现异步置位
  //   正计数到9，倒计数到0时输出为1
endmodule

// 状态转换
module \BCD双向计数器状态转换_自动生成  (
  input  S3,
  input  S2,
  input  S1,
  input  S0,
  input  Mode,
  output N3,
  output N2,
  output N1,
  output N0
);

  wire and_1_out, and_2_out, and_3_out, and_4_out, and_5_out, and_6_out, and_7_out, and_8_out, and_9_out,
       and_10_out, and_11_out, and_12_out, and_13_out, and_14_out, and_15_out, and_16_out, not_1_out,
       not_2_out, not_3_out, not_4_out, not_5_out, not_6_out, not_7_out, not_8_out, not_9_out, not_10_out,
       not_11_out, not_12_out, not_13_out, not_14_out, not_15_out, not_16_out, not_17_out, not_18_out,
       not_19_out, not_20_out, not_21_out, not_22_out, not_23_out, not_24_out, not_25_out, not_26_out,
       not_27_out, not_28_out, not_29_out, not_30_out, not_31_out, not_32_out, not_33_out, not_34_out,
       not_35_out, not_36_out, not_37_out, not_38_out, not_39_out, not_40_out, not_41_out, not_42_out;

  not not_1 (not_1_out, S3);
  not not_2 (not_2_out, S2);
  not not_3 (not_3_out, S1);
  not not_4 (not_4_out, S0);
  not not_5 (not_5_out, S3);
  not not_6 (not_6_out, Mode);
  not not_7 (not_7_out, S2);
  not not_8 (not_8_out, S1);
  not not_9 (not_9_out, S0);
  not not_10 (not_10_out, Mode);
  not not_11 (not_11_out, S2);
  not not_12 (not_12_out, S1);
  not not_13 (not_13_out, S3);
  not not_14 (not_14_out, S2);
  not not_15 (not_15_out, Mode);
  not not_16 (not_16_out, S3);
  not not_17 (not_17_out, S1);
  not not_18 (not_18_out, Mode);
  not not_19 (not_19_out, S3);
  not not_20 (not_20_out, S3);
  not not_21 (not_21_out, S0);
  not not_22 (not_22_out, S2);
  not not_23 (not_23_out, S1);
  not not_24 (not_24_out, S0);
  not not_25 (not_25_out, S3);
  not not_26 (not_26_out, S1);
  not not_27 (not_27_out, Mode);
  not not_28 (not_28_out, S3);
  not not_29 (not_29_out, S0);
  not not_30 (not_30_out, Mode);
  not not_31 (not_31_out, S3);
  not not_32 (not_32_out, S3);
  not not_33 (not_33_out, S1);
  not not_34 (not_34_out, S0);
  not not_35 (not_35_out, S2);
  not not_36 (not_36_out, S1);
  not not_37 (not_37_out, S0);
  not not_38 (not_38_out, S3);
  not not_39 (not_39_out, S0);
  not not_40 (not_40_out, S2);
  not not_41 (not_41_out, S1);
  not not_42 (not_42_out, S0);
  and and_1 (and_1_out, not_1_out, not_2_out, not_3_out, not_4_out, Mode);
  and and_2 (and_2_out, not_5_out, S2, S1, S0, not_6_out);
  and and_3 (and_3_out, S3, not_7_out, not_8_out, not_9_out, not_10_out);
  and and_4 (and_4_out, S3, not_11_out, not_12_out, S0, Mode);
  and and_5 (and_5_out, not_13_out, not_14_out, S1, S0, not_15_out);
  and and_6 (and_6_out, not_16_out, S2, not_17_out, not_18_out);
  and and_7 (and_7_out, not_19_out, S2, S0, Mode);
  and and_8 (and_8_out, not_20_out, S2, S1, not_21_out);
  and and_9 (and_9_out, S3, not_22_out, not_23_out, not_24_out, Mode);
  and and_10 (and_10_out, not_25_out, not_26_out, S0, not_27_out);
  and and_11 (and_11_out, not_28_out, S1, not_29_out, not_30_out);
  and and_12 (and_12_out, not_31_out, S1, S0, Mode);
  and and_13 (and_13_out, not_32_out, S2, not_33_out, not_34_out, Mode);
  and and_14 (and_14_out, S3, not_35_out, not_36_out, not_37_out, Mode);
  and and_15 (and_15_out, not_38_out, not_39_out);
  and and_16 (and_16_out, not_40_out, not_41_out, not_42_out);
  or or_1 (N3, and_1_out, and_2_out, and_3_out, and_4_out);
  or or_2 (N2, and_5_out, and_6_out, and_7_out, and_8_out, and_9_out);
  or or_3 (N1, and_10_out, and_11_out, and_12_out, and_13_out, and_14_out);
  or or_4 (N0, and_15_out, and_16_out);
endmodule

module \BCD双向计数器输出函数_自动生成  (
  input  S3,
  input  S2,
  input  S1,
  input  S0,
  input  Mode,
  output Cout
);

  wire and_1_out, and_2_out, not_1_out, not_2_out, not_3_out, not_4_out, not_5_out, not_6_out, not_7_out;

  not not_1 (not_1_out, S3);
  not not_2 (not_2_out, S2);
  not not_3 (not_3_out, S1);
  not not_4 (not_4_out, S0);
  not not_5 (not_5_out, S2);
  not not_6 (not_6_out, S1);
  not not_7 (not_7_out, Mode);
  and and_1 (and_1_out, not_1_out, not_2_out, not_3_out, not_4_out, Mode);
  and and_2 (and_2_out, S3, not_5_out, not_6_out, S0, not_7_out);
  or or_1 (Cout, and_1_out, and_2_out);
endmodule

// 0~5计数
module \_0_5双向计数器_可异步置位  (
  input  CLK,
  input  \使能 ,
  input  \异步置位 ,
  input  [3:0] \预置数据 ,
  input  \计数模式 ,
  input  RST,
  output [3:0] \输出Q ,
  output \进位_借位 
);

  wire D0, D1, D2, D3, not_1_out, not_2_out, not_3_out, not_4_out, or_1_out;
  wire [3:0] \n0_5双向计数器状态转换_自动生成_1_n0 , \n2路选择器_4位_1_out ;

  Pull_Resistor #(.pull(0)) pull_resistor_1 (.node(\异步置位 ));
  Pull_Resistor #(.pull(0)) pull_resistor_2 (.node(\计数模式 ));
  \_0_5双向计数器输出函数_自动生成  \u_0_5双向计数器输出函数_自动生成_1  (
    .S3(\输出Q [3]), .S2(\输出Q [2]), .S1(\输出Q [1]), .Cout(\进位_借位 ), .S0(\输出Q [0]), .Mode(\计数模式 ));
  \_0_5双向计数器状态转换_自动生成  \u_0_5双向计数器状态转换_自动生成_1  (
    .S3(\输出Q [3]), .N3(\n0_5双向计数器状态转换_自动生成_1_n0 [3]), .S2(\输出Q [2]), .S1(\输出Q [1]), .S0(\输出Q [0]),
    .Mode(\计数模式 ), .N2(\n0_5双向计数器状态转换_自动生成_1_n0 [2]), .N1(\n0_5双向计数器状态转换_自动生成_1_n0 [1]),
    .N0(\n0_5双向计数器状态转换_自动生成_1_n0 [0]));
  Pull_Resistor #(.pull(1)) pull_resistor_3 (.node(\使能 ));
  Pull_Resistor #(.pull(0)) pull_resistor_4 (.node(\预置数据 ));
  Pull_Resistor #(.pull(0)) pull_resistor_5 (.node(RST));
  D_Flip_Flop #(.trigger("rising"), .Pre_Clr_Positions("LEGACY"), .NegatePresetClear("false"), .enable("true"), .NewFFLayout("false")) u_D3 (
    .clk(CLK), .D(\n0_5双向计数器状态转换_自动生成_1_n0 [3]), .Q(\输出Q [3]), .preset(D3), .en(\使能 ), .reset(not_1_out));  // open: Qn
  not not_1 (not_1_out, D3);
  D_Flip_Flop #(.trigger("rising"), .Pre_Clr_Positions("LEGACY"), .NegatePresetClear("false"), .enable("true"), .NewFFLayout("false")) u_D2 (
    .clk(CLK), .D(\n0_5双向计数器状态转换_自动生成_1_n0 [2]), .Q(\输出Q [2]), .preset(D2), .en(\使能 ), .reset(not_2_out));  // open: Qn
  not not_2 (not_2_out, D2);
  D_Flip_Flop #(.trigger("rising"), .Pre_Clr_Positions("LEGACY"), .NegatePresetClear("false"), .enable("true"), .NewFFLayout("false")) u_D1 (
    .clk(CLK), .D(\n0_5双向计数器状态转换_自动生成_1_n0 [1]), .Q(\输出Q [1]), .preset(D1), .en(\使能 ), .reset(not_3_out));  // open: Qn
  not not_3 (not_3_out, D1);
  D_Flip_Flop #(.trigger("rising"), .Pre_Clr_Positions("LEGACY"), .NegatePresetClear("false"), .enable("true"), .NewFFLayout("false")) u_D0 (
    .clk(CLK), .D(\n0_5双向计数器状态转换_自动生成_1_n0 [0]), .Q(\输出Q [0]), .preset(D0), .en(\使能 ), .reset(not_4_out));  // open: Qn
  not not_4 (not_4_out, D0);
  \_2路选择器_4位  \u_2路选择器_4位_1  (.X(\预置数据 ), .Out(\n2路选择器_4位_1_out ), .Sel(RST), .Y(4'b0000));
  assign {D3, D2, D1, D0} = or_1_out ? \n2路选择器_4位_1_out  : 4'bz;  // Controlled_Buffer controlled_buffer_1
  or or_1 (or_1_out, RST, \异步置位 );
  // Probe on \输出Q 

  // Other names for the same wires on the sheet: Cout = \进位_借位 ; Din[3:0] = \预置数据 ; En = \使能 ; Mode = \计数模式 ;
  //   PreSet = \异步置位 ; Q[3:0] = \输出Q 

  // Notes on the sheet:
  //   请勿增删改引脚，否则可能导致电路封装变化，无法测试！！！
  //   上拉下拉电阻用于给出引脚悬空的时的默认值
  //   D3D2D1D0分别接D触发器异步置位和复位端实现异步置位
  //   正计数到9，倒计数到0时输出为1
endmodule

// 状态转换
module \_0_5双向计数器状态转换_自动生成  (
  input  S3,
  input  S2,
  input  S1,
  input  S0,
  input  Mode,
  output N3,
  output N2,
  output N1,
  output N0
);

  wire and_1_out, and_2_out, and_3_out, and_4_out, and_5_out, and_6_out, and_7_out, and_8_out, and_9_out,
       and_10_out, not_1_out, not_2_out, not_3_out, not_4_out, not_5_out, not_6_out, not_7_out, not_8_out,
       not_9_out, not_10_out, not_11_out, not_12_out, not_13_out, not_14_out, not_15_out, not_16_out,
       not_17_out, not_18_out, not_19_out, not_20_out, not_21_out, not_22_out, not_23_out, not_24_out,
       not_25_out, not_26_out, not_27_out, not_28_out, not_29_out, not_30_out, not_31_out, not_32_out;

  not not_1 (not_1_out, S3);
  not not_2 (not_2_out, S2);
  not not_3 (not_3_out, S1);
  not not_4 (not_4_out, S0);
  not not_5 (not_5_out, S3);
  not not_6 (not_6_out, S2);
  not not_7 (not_7_out, Mode);
  not not_8 (not_8_out, S3);
  not not_9 (not_9_out, S1);
  not not_10 (not_10_out, S0);
  not not_11 (not_11_out, Mode);
  not not_12 (not_12_out, S3);
  not not_13 (not_13_out, S1);
  not not_14 (not_14_out, S3);
  not not_15 (not_15_out, S2);
  not not_16 (not_16_out, S1);
  not not_17 (not_17_out, Mode);
  not not_18 (not_18_out, S3);
  not not_19 (not_19_out, S2);
  not not_20 (not_20_out, S0);
  not not_21 (not_21_out, Mode);
  not not_22 (not_22_out, S3);
  not not_23 (not_23_out, S2);
  not not_24 (not_24_out, S3);
  not not_25 (not_25_out, S1);
  not not_26 (not_26_out, S0);
  not not_27 (not_27_out, S3);
  not not_28 (not_28_out, S2);
  not not_29 (not_29_out, S0);
  not not_30 (not_30_out, S3);
  not not_31 (not_31_out, S1);
  not not_32 (not_32_out, S0);
  and and_1 (and_1_out, not_1_out, not_2_out, not_3_out, not_4_out, Mode);
  and and_2 (and_2_out, not_5_out, not_6_out, S1, S0, not_7_out);
  and and_3 (and_3_out, not_8_out, S2, not_9_out, not_10_out, not_11_out);
  and and_4 (and_4_out, not_12_out, S2, not_13_out, S0, Mode);
  and and_5 (and_5_out, not_14_out, not_15_out, not_16_out, S0, not_17_out);
  and and_6 (and_6_out, not_18_out, not_19_out, S1, not_20_out, not_21_out);
  and and_7 (and_7_out, not_22_out, not_23_out, S1, S0, Mode);
  and and_8 (and_8_out, not_24_out, S2, not_25_out, not_26_out, Mode);
  and and_9 (and_9_out, not_27_out, not_28_out, not_29_out);
  and and_10 (and_10_out, not_30_out, not_31_out, not_32_out);
  or or_1 (N2, and_1_out, and_2_out, and_3_out, and_4_out);
  or or_2 (N1, and_5_out, and_6_out, and_7_out, and_8_out);
  or or_3 (N0, and_9_out, and_10_out);

  assign N3 = 1'b0;
endmodule

module \_0_5双向计数器输出函数_自动生成  (
  input  S3,
  input  S2,
  input  S1,
  input  S0,
  input  Mode,
  output Cout
);

  wire and_1_out, and_2_out, not_1_out, not_2_out, not_3_out, not_4_out, not_5_out, not_6_out, not_7_out;

  not not_1 (not_1_out, S3);
  not not_2 (not_2_out, S2);
  not not_3 (not_3_out, S1);
  not not_4 (not_4_out, S0);
  not not_5 (not_5_out, S3);
  not not_6 (not_6_out, S1);
  not not_7 (not_7_out, Mode);
  and and_1 (and_1_out, not_1_out, not_2_out, not_3_out, not_4_out, Mode);
  and and_2 (and_2_out, not_5_out, S2, not_6_out, S0, not_7_out);
  or or_1 (Cout, and_1_out, and_2_out);
endmodule

// 0~59双向计数
module \_0_59双向计数器  (
  input  CLK,
  input  \使能 ,
  input  \异步置位 ,
  input  [7:0] \预置数据 ,
  input  \计数模式 ,
  input  RST,
  output [7:0] \输出Q ,
  output \进位_借位 
);

  wire and_1_out, \bcd双向计数器_可异步置位_1_进位_借位 , \n0_5双向计数器_可异步置位_1_进位_借位 ;

  Pull_Resistor #(.pull(0)) pull_resistor_1 (.node(\异步置位 ));
  Pull_Resistor #(.pull(0)) pull_resistor_2 (.node(\计数模式 ));
  and and_1 (and_1_out, \使能 , \bcd双向计数器_可异步置位_1_进位_借位 );
  \_0_5双向计数器_可异步置位  \u_0_5双向计数器_可异步置位_1  (
    .CLK(CLK), .\使能 (and_1_out), .\异步置位 (\异步置位 ), .\预置数据 (\预置数据 [7:4]), .\计数模式 (\计数模式 ), .\输出Q (\输出Q [7:4]),
    .\进位_借位 (\n0_5双向计数器_可异步置位_1_进位_借位 ), .RST(RST));
  Pull_Resistor #(.pull(1)) pull_resistor_3 (.node(\使能 ));
  Pull_Resistor #(.pull(0)) pull_resistor_4 (.node(\预置数据 ));
  Pull_Resistor #(.pull(0)) pull_resistor_5 (.node(RST));
  \BCD双向计数器_可异步置位  \bcd双向计数器_可异步置位_1  (
    .CLK(CLK), .\使能 (\使能 ), .\输出Q (\输出Q [3:0]), .\异步置位 (\异步置位 ), .\预置数据 (\预置数据 [3:0]),
    .\进位_借位 (\bcd双向计数器_可异步置位_1_进位_借位 ), .\计数模式 (\计数模式 ), .\复位 (RST));
  and and_2 (\进位_借位 , \n0_5双向计数器_可异步置位_1_进位_借位 , \bcd双向计数器_可异步置位_1_进位_借位 );

  // Other names for the same wires on the sheet: Cout = \进位_借位 ; Din[7:0] = \预置数据 ; Din0[3:0] = \预置数据 [3:0];
  //   Din1[3:0] = \预置数据 [7:4]; En = \使能 ; Mode = \计数模式 ; PreSet = \异步置位 ; Q[7:0] = \输出Q 

  // Notes on the sheet:
  //   请勿增删改引脚，否则可能导致电路封装变化，无法测试！！！
  //   正计数到59，倒计数到0时输出为1
endmodule

// 倒计数
module \_59分59秒双向计数器  (
  input  CLK,
  input  \使能 ,
  input  \异步置位 ,
  input  [15:0] \预置数据 ,
  input  \计数模式 ,
  input  RST,
  output [7:0] Minute,
  output [7:0] Second,
  output \进位_借位 
);

  Pull_Resistor #(.pull(0)) pull_resistor_1 (.node(\异步置位 ));
  Pull_Resistor #(.pull(0)) pull_resistor_2 (.node(\计数模式 ));
  \_0_59双向计数器  \u_0_59双向计数器_1  ();  // open: CLK, 使能, 输出Q, 异步置位, 预置数据, 进位_借位, 计数模式, RST
  Pull_Resistor #(.pull(1)) pull_resistor_3 (.node(\使能 ));
  Pull_Resistor #(.pull(0)) pull_resistor_4 (.node(\预置数据 ));
  Pull_Resistor #(.pull(0)) pull_resistor_5 (.node(RST));
  \_0_59双向计数器  \u_0_59双向计数器_2  ();  // open: CLK, 使能, 输出Q, 异步置位, 预置数据, 进位_借位, 计数模式, RST

  // Other names for the same wires on the sheet: Cout = \进位_借位 ; Din[15:0] = \预置数据 ; SDin[7:0] = \预置数据 [7:0];
  //   MDin[7:0] = \预置数据 [15:8]; En = \使能 ; Min[7:0] = Minute; Mode = \计数模式 ; PreSet = \异步置位 ; Sec[7:0] = Second

  // Notes on the sheet:
  //   请勿增删改引脚，否则可能导致电路封装变化，无法测试！！！
  //   正计数到59：59，倒计数到0时输出为1
endmodule

module \厨房计时器状态机  (
  input  S2,
  input  S1,
  input  S0,
  input  mode,
  input  start,
  input  timer,
  input  finished,
  output N2,
  output N1,
  output N0
);
endmodule

module \厨房计时器输出函数  (
  input  S2,
  input  S1,
  input  S0,
  output Preset,
  output CounterEn,
  output AlertTimerEnable,
  output Runing
);
endmodule

module \厨房计数器  (
);

  wire _0_5HZ, _1HZ, _16HZ, Alert, undriven, \分 , \开始_暂停 , \归零 , \时间到 , \秒 ;
  wire [0:0] counter_1_q;
  wire [2:0] S1B, S2B, S3B, S4B;
  wire [3:0] S1T, S2T, S3T, S4T;

  _7_Segment_Display #(.active("true")) u_7_segment_display_1 (
    .g(S4T[0]), .f(S4T[1]), .a(S4T[2]), .b(S4T[3]), .e(S4B[0]), .d(S4B[1]), .c(S4B[2]));  // open: dp
  _7_Segment_Display #(.active("true")) u_7_segment_display_2 (
    .g(S2T[0]), .f(S2T[1]), .a(S2T[2]), .b(S2T[3]), .e(S2B[0]), .d(S2B[1]), .c(S2B[2]));  // open: dp
  _7_Segment_Display #(.active("true")) u_7_segment_display_3 (
    .g(S3T[0]), .f(S3T[1]), .a(S3T[2]), .b(S3T[3]), .e(S3B[0]), .d(S3B[1]), .c(S3B[2]));  // open: dp
  Button button_1 (.out(\分 ));
  _7_Segment_Display #(.active("true")) u_7_segment_display_4 (
    .g(S1T[0]), .f(S1T[1]), .a(S1T[2]), .b(S1T[3]), .e(S1B[0]), .d(S1B[1]), .c(S1B[2]));  // open: dp
  Button button_2 (.out(\开始_暂停 ));
  Button button_3 (.out(\秒 ));
  Button button_4 (.out(\归零 ));
  Clock #(.highDuration(1), .lowDuration(1)) clock_1 (.out(_16HZ));
  Counter #(.width(3), .max('h7), .ongoal("wrap"), .trigger("rising"), .behavior("new")) counter_1 (
    .count(undriven), .Q({_1HZ, _0_5HZ, counter_1_q[0]}), .clk(_16HZ), .preset(undriven));  // open: load, D, carry, clr, down
  and and_1 (\时间到 , Alert, _1HZ);
  // Buzzer #(.freq_measure("Hz"), .vol_width(7)) buzzer_1: pin names not known; wires that end beside it: 14'h1000, \时间到 , {7{1'b1}}

  // Notes on the sheet:
  //   厨房计时器
  //   分频电路
  //   蜂鸣器
endmodule
